// Logisim project Computer.circ as structural Verilog
module CPU (
);

  wire A_I, ADD, AO, B_I, BO, CE, CLO, clock_1_clock, CO, DIV, HLT, I_I, IO, J, JEQ, JGR, JLS, JNQ, JU, M_I,
       MO, MUL, not_1_out, OUT, RE, SUB, tunnel, tunnel_t, tunnel_t_t, WR;
  wire [3:0] n4_digit_decimal_display_1_out_2, n4_digit_decimal_display_1_out_3,
       n4_digit_decimal_display_1_out_4, n4_digit_decimal_display_1_out_5, n4_digit_decimal_display_2_out_2,
       n4_digit_decimal_display_2_out_3, n4_digit_decimal_display_2_out_4, n4_digit_decimal_display_2_out_5,
       n4_digit_decimal_display_3_out_2, n4_digit_decimal_display_3_out_3, n4_digit_decimal_display_3_out_4,
       n4_digit_decimal_display_3_out_5, n4_digit_decimal_display_4_out_2, n4_digit_decimal_display_4_out_3,
       n4_digit_decimal_display_4_out_4, n4_digit_decimal_display_4_out_5, n4_digit_decimal_display_5_out_2,
       n4_digit_decimal_display_5_out_3, n4_digit_decimal_display_5_out_4, n4_digit_decimal_display_5_out_5,
       n4_digit_decimal_display_6_out_2, n4_digit_decimal_display_6_out_3, n4_digit_decimal_display_6_out_4,
       n4_digit_decimal_display_6_out_5;
  wire [7:0] instruction_register_1_machine_code, OUT_IN;
  wire [15:0] alu_1_alu_out, Operand, or_1_out, or_3_out, or_4_out, or_5_out, Out0, Out1, Out2, Out3, Out4,
       Out5, output_register_1_output_g, output_register_1_output_h, program_counter_1_out_7,
       program_counter_1_output_address, register_1_register_out, register_2_register_out, RO;
  wire [23:0] program_memory_1_program_instruction;

  assign or_1_out = register_1_register_out | register_2_register_out;  // OR_Gate or_1, 16 bits wide
  // Probe on register_1_register_out
  // Probe on register_2_register_out
  assign OUT_IN = RO[7:0] | Operand[7:0];  // OR_Gate or_2, 8 bits wide
  Register register_1 (
    .Register_In(or_3_out), .A_I(A_I), .AO(AO), .Clock(clock_1_clock), .Register_Out(register_1_register_out));
  Register register_2 (
    .Register_In(or_4_out), .A_I(B_I), .AO(BO), .Clock(clock_1_clock), .Register_Out(register_2_register_out));
  RAM_Module ram_module_1 (
    .RAM_Address(Operand), .MI(M_I), .Write_Value(or_1_out), .WR(WR), .Clock(clock_1_clock), .MO(MO),
    .RAM_Output(RO));
  Output_Register output_register_1 (
    .Operand(OUT_IN), .Output(or_1_out), .Clock(clock_1_clock), .Clear(CLO), .Output_A(Out0),
    .Output_B(Out1), .Output_C(Out2), .Output_D(Out3), .Output_E(Out4), .Output_F(Out5),
    .Output_G(output_register_1_output_g), .Output_H(output_register_1_output_h), .Output_Enable(OUT));
  Clock clock_1 (.HLT(HLT), .Clock(clock_1_clock));
  ALU alu_1 (
    .Add_Out(ADD), .Sub_Out(SUB), .Mul_Out(MUL), .Div_Out(DIV), .ALU_Out(alu_1_alu_out), .out_8(tunnel_t_t),
    .out_9(tunnel_t), .out_10(tunnel), .Register_A(register_1_register_out),
    .Register_B(register_2_register_out));
  assign or_3_out = alu_1_alu_out | Operand | RO;  // OR_Gate or_3, 16 bits wide
  assign or_4_out = Operand | RO;  // OR_Gate or_4, 16 bits wide
  assign or_5_out = RO | Operand;  // OR_Gate or_5, 16 bits wide
  // Probe on RO
  Program_Counter program_counter_1 (
    .Instruction_Address(or_5_out), .Counter_Out(CO), .Jump(JU), .Counter_Enable(CE), .Clock(clock_1_clock),
    .Output_Address(program_counter_1_output_address), .out_7(program_counter_1_out_7));
  Instruction_Register instruction_register_1 (
    .Program_Instruction(program_memory_1_program_instruction), .Instruction_In(I_I), .Clock(clock_1_clock),
    .Instruction_Out(IO), .Machine_Code(instruction_register_1_machine_code), .Operand(Operand));
  not not_1 (not_1_out, clock_1_clock);
  // Probe on program_counter_1_out_7
  Program_Memory program_memory_1 (
    .Program_Count(program_counter_1_output_address),
    .Program_Instruction(program_memory_1_program_instruction));
  MicroInstruction_Processor microinstruction_processor_1 (
    .Machine_Code(instruction_register_1_machine_code),
    .MicroInstruction({I_I, IO, CE, CO, OUT, CLO, HLT, RE, ADD, SUB, MUL, DIV, A_I, AO, B_I, BO, M_I, MO, WR, J, JEQ, JNQ, JLS, JGR}),
    .Clock(not_1_out), .RE(RE));
  Jump_Circuit jump_circuit_1 (
    .in_1(tunnel_t_t), .in_2(tunnel_t), .in_3(tunnel), .JEQ(JEQ), .JNQ(JNQ), .JLS(JLS), .JGR(JGR),
    .out_9(JU), .J(J));
  // Probe on instruction_register_1_machine_code
  // Probe on program_memory_1_program_instruction
  // Probe on {I_I, IO, CE, CO, OUT, CLO, HLT, RE, ADD, SUB, MUL, DIV, A_I, AO, B_I, BO, M_I, MO, WR, J, JEQ, JNQ, JLS, JGR}
  _4_Digit_Decimal_Display u_4_digit_decimal_display_1 (
    ._16bit_Input(Out0), .out_2(n4_digit_decimal_display_1_out_2), .out_3(n4_digit_decimal_display_1_out_3),
    .out_4(n4_digit_decimal_display_1_out_4), .out_5(n4_digit_decimal_display_1_out_5));
  _4_Digit_Decimal_Display u_4_digit_decimal_display_2 (
    ._16bit_Input(Out1), .out_2(n4_digit_decimal_display_2_out_2), .out_3(n4_digit_decimal_display_2_out_3),
    .out_4(n4_digit_decimal_display_2_out_4), .out_5(n4_digit_decimal_display_2_out_5));
  _4_Digit_Decimal_Display u_4_digit_decimal_display_3 (
    ._16bit_Input(Out2), .out_2(n4_digit_decimal_display_3_out_2), .out_3(n4_digit_decimal_display_3_out_3),
    .out_4(n4_digit_decimal_display_3_out_4), .out_5(n4_digit_decimal_display_3_out_5));
  _4_Digit_Decimal_Display u_4_digit_decimal_display_4 (
    ._16bit_Input(Out3), .out_2(n4_digit_decimal_display_4_out_2), .out_3(n4_digit_decimal_display_4_out_3),
    .out_4(n4_digit_decimal_display_4_out_4), .out_5(n4_digit_decimal_display_4_out_5));
  _4_Digit_Decimal_Display u_4_digit_decimal_display_5 (
    ._16bit_Input(Out4), .out_2(n4_digit_decimal_display_5_out_2), .out_3(n4_digit_decimal_display_5_out_3),
    .out_4(n4_digit_decimal_display_5_out_4), .out_5(n4_digit_decimal_display_5_out_5));
  _4_Digit_Decimal_Display u_4_digit_decimal_display_6 (
    ._16bit_Input(Out5), .out_2(n4_digit_decimal_display_6_out_2), .out_3(n4_digit_decimal_display_6_out_3),
    .out_4(n4_digit_decimal_display_6_out_4), .out_5(n4_digit_decimal_display_6_out_5));
  Hex_Digit_Display hex_digit_display_1 (.value(n4_digit_decimal_display_1_out_3));  // open: dp
  Hex_Digit_Display hex_digit_display_2 (.value(n4_digit_decimal_display_1_out_2));  // open: dp
  Hex_Digit_Display hex_digit_display_3 (.value(n4_digit_decimal_display_2_out_2));  // open: dp
  Hex_Digit_Display hex_digit_display_4 (.value(n4_digit_decimal_display_2_out_3));  // open: dp
  Hex_Digit_Display hex_digit_display_5 (.value(n4_digit_decimal_display_3_out_2));  // open: dp
  Hex_Digit_Display hex_digit_display_6 (.value(n4_digit_decimal_display_3_out_3));  // open: dp
  Hex_Digit_Display hex_digit_display_7 (.value(n4_digit_decimal_display_4_out_3));  // open: dp
  Hex_Digit_Display hex_digit_display_8 (.value(n4_digit_decimal_display_4_out_2));  // open: dp
  Hex_Digit_Display hex_digit_display_9 (.value(n4_digit_decimal_display_5_out_2));  // open: dp
  Hex_Digit_Display hex_digit_display_10 (.value(n4_digit_decimal_display_5_out_3));  // open: dp
  Hex_Digit_Display hex_digit_display_11 (.value(n4_digit_decimal_display_6_out_2));  // open: dp
  Hex_Digit_Display hex_digit_display_12 (.value(n4_digit_decimal_display_6_out_3));  // open: dp
  Hex_Digit_Display hex_digit_display_13 (.value(n4_digit_decimal_display_1_out_5));  // open: dp
  Hex_Digit_Display hex_digit_display_14 (.value(n4_digit_decimal_display_1_out_4));  // open: dp
  Hex_Digit_Display hex_digit_display_15 (.value(n4_digit_decimal_display_2_out_4));  // open: dp
  Hex_Digit_Display hex_digit_display_16 (.value(n4_digit_decimal_display_2_out_5));  // open: dp
  Hex_Digit_Display hex_digit_display_17 (.value(n4_digit_decimal_display_3_out_5));  // open: dp
  Hex_Digit_Display hex_digit_display_18 (.value(n4_digit_decimal_display_3_out_4));  // open: dp
  Hex_Digit_Display hex_digit_display_19 (.value(n4_digit_decimal_display_4_out_4));  // open: dp
  Hex_Digit_Display hex_digit_display_20 (.value(n4_digit_decimal_display_4_out_5));  // open: dp
  Hex_Digit_Display hex_digit_display_21 (.value(n4_digit_decimal_display_5_out_5));  // open: dp
  Hex_Digit_Display hex_digit_display_22 (.value(n4_digit_decimal_display_5_out_4));  // open: dp
  Hex_Digit_Display hex_digit_display_23 (.value(n4_digit_decimal_display_6_out_4));  // open: dp
  Hex_Digit_Display hex_digit_display_24 (.value(n4_digit_decimal_display_6_out_5));  // open: dp

  // Notes on the sheet:
  //   Register A
  //   Register B
endmodule

module Program_Counter (
  input  [15:0] Instruction_Address,
  input  Counter_Out,
  input  Jump,
  input  Counter_Enable,
  input  Clock,
  output [15:0] Output_Address,
  output [15:0] out_7
);

  Counter #(.width(16), .max('hffff)) counter_1 (
    .load(Jump), .D(Instruction_Address), .count(Counter_Enable), .Q(out_7), .clk(Clock));  // open: carry, clr
  assign Output_Address = {16{Counter_Out}} & out_7;  // AND_Gate and_1, 16 bits wide
endmodule

module Instruction_Register (
  input  [23:0] Program_Instruction,
  input  Instruction_In,
  input  Clock,
  input  Instruction_Out,
  output [7:0] Machine_Code,
  output [15:0] Operand
);

  wire [15:0] register_1_q;

  Register_part #(.width(24)) register_1 (
    .D(Program_Instruction), .en(Instruction_In), .Q({Machine_Code, register_1_q}), .clk(Clock));  // open: clr
  assign Operand = register_1_q & {16{Instruction_Out}};  // AND_Gate and_1, 16 bits wide
endmodule

module MicroInstruction_Processor (
  input  [7:0] Machine_Code,
  input  Clock,
  input  RE,
  output [23:0] MicroInstruction
);

  wire [2:0] counter_1_q;

  Counter #(.width(3), .max('h7)) counter_1 (.Q(counter_1_q), .clk(Clock), .clr(RE));  // open: load, D, count, carry
  // Probe on {Machine_Code, counter_1_q}
  ROM #(.addrWidth(11), .dataWidth(24)) rom_1 (
    .addr({Machine_Code, counter_1_q}), .data(MicroInstruction));  // open: sel

  // Notes on the sheet:
  //   contents of rom_1 (hex, n*v repeats v):
  //   900000 220000 10000 5*0 900000 600080 840 10000 4*0 900000 6004a0 10000 5*0 900000 600080 240 10000
  //   4*0 900000 6001a0 10000 5*0 900000 600800 10000 5*0 900000 600200 10000 5*0 900000 208d00 10000 5*0
  //   900000 204d00 10000 5*0 900000 202d00 10000 5*0 900000 201d00 10000 5*0 900000 0 10000 5*0 900000
  //   400010 10000 5*0 900000 200000 400508 10000 4*0 900000 200000 400504 10000 4*0 900000 200000 400502
  //   10000 4*0 900000 200000 400501 10000 4*0 900000 680400 10000 5*0 900000 680100 10000 5*0 900000
  //   600081 51 10000 4*0 900000 200480 840 10000 4*0 900000 200180 240 10000 4*0 900000 600080 80440
  //   10000 4*0 900000 600080 80140 10000 4*0 900000 200180 420 10000 4*0 900000 200480 120 10000 4*0
  //   900000 7*0 900000 7*0 900000 7*0 900000 7*0 900000 7*0 900000 7*0 900000 7*0 900000 7*0 900000
endmodule

module Program_Memory (
  input  [15:0] Program_Count,
  output [23:0] Program_Instruction
);

  ROM #(.addrWidth(16), .dataWidth(24)) rom_1 (.addr(Program_Count), .data(Program_Instruction));  // open: sel

  // Notes on the sheet:
  //   Program Memory
  //   contents of rom_1 (hex, n*v repeats v):
  //   c000b 10005 30006 100006 d0006 c0009 80000 20005 c0003 20007 130008 50000 20000 60001 40001 60000
  //   40003 6270f 40004 10000 30004 f0018 d0018 c002c 160003 10001 20002 30000 70000 20001 10002 20000
  //   10003 60001 70000 20005 60006 40006 60029 40008 c0001 10007 20003 c0013
endmodule

module Register (
  input  [15:0] Register_In,
  input  A_I,
  input  AO,
  input  Clock,
  output [15:0] Register_Out
);

  wire [15:0] register_1_q;

  Register_part #(.width(16)) register_1 (.D(Register_In), .en(A_I), .Q(register_1_q), .clk(Clock));  // open: clr
  assign Register_Out = register_1_q & {16{AO}};  // AND_Gate and_1, 16 bits wide
endmodule

module ALU (
  input  [15:0] Register_A,
  input  [15:0] Register_B,
  input  Add_Out,
  input  Sub_Out,
  input  Mul_Out,
  input  Div_Out,
  output [15:0] ALU_Out,
  output out_8,
  output out_9,
  output out_10
);

  wire [15:0] adder_1_out, and_1_out, and_2_out, and_3_out, and_4_out, divider_1_out, multiplier_1_out,
       subtractor_1_out;

  Adder #(.width(16)) adder_1 (.a(Register_A), .b(Register_B), .out(adder_1_out));  // open: cin, cout
  Subtractor #(.width(16)) subtractor_1 (.a(Register_A), .b(Register_B), .out(subtractor_1_out));  // open: bin, bout
  Multiplier #(.width(16)) multiplier_1 (.a(Register_A), .b(Register_B), .out(multiplier_1_out));  // open: cin, cout
  Divider #(.width(16)) divider_1 (.a(Register_A), .b(Register_B), .out(divider_1_out));  // open: upper, rem
  Comparator #(.width(16)) comparator_1 (.a(Register_A), .b(Register_B), .gt(out_8), .eq(out_9), .lt(out_10));
  assign and_1_out = adder_1_out & {16{Add_Out}};  // AND_Gate and_1, 16 bits wide
  assign and_2_out = subtractor_1_out & {16{Sub_Out}};  // AND_Gate and_2, 16 bits wide
  assign and_3_out = multiplier_1_out & {16{Mul_Out}};  // AND_Gate and_3, 16 bits wide
  assign and_4_out = divider_1_out & {16{Div_Out}};  // AND_Gate and_4, 16 bits wide
  assign ALU_Out = and_1_out | and_2_out | and_3_out | and_4_out;  // OR_Gate or_1, 16 bits wide
endmodule

module Clock (
  input  HLT,
  output Clock
);

  wire Clock_out, d_ff_1_q, d_ff_1_qn, not_1_out;

  Clock_part u_Clock (.out(Clock_out));
  not not_1 (not_1_out, d_ff_1_q);
  and and_1 (Clock, Clock_out, d_ff_1_qn);
  D_Flip_Flop d_ff_1 (.clk(Clock_out), .D(HLT), .Q(d_ff_1_q), .Qn(d_ff_1_qn), .en(not_1_out));  // open: preset, reset
endmodule

module RAM_Module (
  input  [15:0] RAM_Address,
  input  MI,
  input  [15:0] Write_Value,
  input  WR,
  input  Clock,
  input  MO,
  output [15:0] RAM_Output
);

  wire not_1_out;
  wire [15:0] ram_1_data, register_1_q;

  Register_part #(.width(16)) register_1 (.D(RAM_Address), .en(MI), .Q(register_1_q), .clk(Clock));  // open: clr
  RAM #(.addrWidth(16), .dataWidth(16), .bus("separate")) ram_1 (
    .addr(register_1_q), .din(Write_Value), .data(ram_1_data), .str(WR), .clk(not_1_out));  // open: sel, ld, clr
  not not_1 (not_1_out, Clock);
  assign RAM_Output = ram_1_data & {16{MO}};  // AND_Gate and_1, 16 bits wide
endmodule

module Output_Register (
  input  [7:0] Operand,
  input  [15:0] Output,
  input  Clock,
  input  Clear,
  input  Output_Enable,
  output [15:0] Output_A,
  output [15:0] Output_B,
  output [15:0] Output_C,
  output [15:0] Output_D,
  output [15:0] Output_E,
  output [15:0] Output_F,
  output [15:0] Output_G,
  output [15:0] Output_H
);

  wire and_1_out, and_2_out, and_3_out, and_4_out, and_5_out, and_6_out, and_7_out, and_8_out, and_9_out,
       and_10_out, and_11_out, and_12_out, and_13_out, and_14_out, and_15_out, and_16_out;

  and and_1 (and_1_out, ~Operand[0], ~Operand[1], ~Operand[2]);  // AND_Gate
  and and_2 (and_2_out, Operand[0], ~Operand[1], ~Operand[2]);  // AND_Gate
  and and_3 (and_3_out, ~Operand[0], Operand[1], ~Operand[2]);  // AND_Gate
  and and_4 (and_4_out, Operand[0], Operand[1], ~Operand[2]);  // AND_Gate
  and and_5 (and_5_out, ~Operand[0], ~Operand[1], Operand[2]);  // AND_Gate
  and and_6 (and_6_out, Operand[0], ~Operand[1], Operand[2]);  // AND_Gate
  and and_7 (and_7_out, ~Operand[0], Operand[1], Operand[2]);  // AND_Gate
  and and_8 (and_8_out, Operand[1], Operand[2], Operand[0]);
  and and_9 (and_9_out, and_1_out, Output_Enable);
  and and_10 (and_10_out, and_2_out, Output_Enable);
  and and_11 (and_11_out, and_3_out, Output_Enable);
  and and_12 (and_12_out, and_4_out, Output_Enable);
  and and_13 (and_13_out, and_5_out, Output_Enable);
  and and_14 (and_14_out, and_6_out, Output_Enable);
  and and_15 (and_15_out, and_7_out, Output_Enable);
  and and_16 (and_16_out, and_8_out, Output_Enable);
  Register_part #(.width(16)) register_1 (.D(Output), .en(and_9_out), .Q(Output_A), .clk(Clock), .clr(Clear));
  Register_part #(.width(16)) register_2 (.D(Output), .en(and_10_out), .Q(Output_B), .clk(Clock), .clr(Clear));
  Register_part #(.width(16)) register_3 (.D(Output), .en(and_11_out), .Q(Output_C), .clk(Clock), .clr(Clear));
  Register_part #(.width(16)) register_4 (.D(Output), .en(and_12_out), .Q(Output_D), .clk(Clock), .clr(Clear));
  Register_part #(.width(16)) register_5 (.D(Output), .en(and_13_out), .Q(Output_E), .clk(Clock), .clr(Clear));
  Register_part #(.width(16)) register_6 (.D(Output), .en(and_14_out), .Q(Output_F), .clk(Clock), .clr(Clear));
  Register_part #(.width(16)) register_7 (.D(Output), .en(and_15_out), .Q(Output_G), .clk(Clock), .clr(Clear));
  Register_part #(.width(16)) register_8 (.D(Output), .en(and_16_out), .Q(Output_H), .clk(Clock), .clr(Clear));
endmodule

module Jump_Circuit (
  input  in_1,
  input  in_2,
  input  in_3,
  input  JEQ,
  input  JNQ,
  input  JLS,
  input  JGR,
  input  J,
  output out_9
);

  wire and_1_out, and_2_out, and_3_out, and_4_out;

  and and_1 (and_1_out, in_1, JGR);
  and and_2 (and_2_out, in_2, JEQ);
  and and_3 (and_3_out, ~in_2, JNQ);  // AND_Gate
  and and_4 (and_4_out, in_3, JLS);
  or or_1 (out_9, and_1_out, and_2_out, and_3_out, and_4_out, J);
endmodule

module Load_Register (
  input  [7:0] in_1,
  input  LI1,
  input  LI2,
  input  Clock,
  input  LO,
  output [15:0] out_6
);

  wire [7:0] Register_1_q, Register_2_q;

  Register_part Register_1 (.D(in_1), .en(LI1), .Q(Register_1_q), .clk(Clock));  // open: clr
  Register_part Register_2 (.D(in_1), .en(LI2), .Q(Register_2_q), .clk(Clock));  // open: clr
  assign out_6 = {Register_1_q, Register_2_q} & {16{LO}};  // AND_Gate and_1, 16 bits wide
endmodule

module Add_3_Module (
  input  A3,
  input  A2,
  input  A1,
  input  A0,
  output S3,
  output S2,
  output S1,
  output S0
);

  ROM #(.addrWidth(4), .dataWidth(4)) rom_1 (.addr({A3, A2, A1, A0}), .data({S3, S2, S1, S0}));  // open: sel

  // Notes on the sheet:
  //   contents of rom_1 (hex, n*v repeats v):
  //   0 1 2 3 4 8 9 a b c
endmodule

module _4_Digit_Decimal_Display (
  input  [15:0] _16bit_Input,
  output [3:0] out_2,
  output [3:0] out_3,
  output [3:0] out_4,
  output [3:0] out_5
);

  wire add_3_module_1_s0, add_3_module_1_s1, add_3_module_1_s2, add_3_module_1_s3, add_3_module_2_s0,
       add_3_module_2_s1, add_3_module_2_s2, add_3_module_2_s3, add_3_module_3_s0, add_3_module_3_s1,
       add_3_module_3_s2, add_3_module_3_s3, add_3_module_4_s0, add_3_module_4_s1, add_3_module_4_s2,
       add_3_module_4_s3, add_3_module_5_s0, add_3_module_5_s1, add_3_module_5_s2, add_3_module_5_s3,
       add_3_module_6_s0, add_3_module_6_s1, add_3_module_6_s2, add_3_module_6_s3, add_3_module_7_s0,
       add_3_module_7_s1, add_3_module_7_s2, add_3_module_7_s3, add_3_module_8_s0, add_3_module_8_s1,
       add_3_module_8_s2, add_3_module_8_s3, add_3_module_9_s0, add_3_module_9_s1, add_3_module_9_s2,
       add_3_module_9_s3, add_3_module_10_s0, add_3_module_10_s1, add_3_module_10_s2, add_3_module_10_s3,
       add_3_module_11_s0, add_3_module_11_s1, add_3_module_11_s2, add_3_module_11_s3, add_3_module_12_s0,
       add_3_module_12_s1, add_3_module_12_s2, add_3_module_12_s3, add_3_module_13_s0, add_3_module_13_s1,
       add_3_module_13_s2, add_3_module_13_s3, add_3_module_14_s0, add_3_module_14_s1, add_3_module_14_s2,
       add_3_module_14_s3, add_3_module_15_s0, add_3_module_15_s1, add_3_module_15_s2, add_3_module_15_s3,
       add_3_module_16_s0, add_3_module_16_s1, add_3_module_16_s2, add_3_module_16_s3, add_3_module_17_s0,
       add_3_module_17_s1, add_3_module_17_s2, add_3_module_17_s3, add_3_module_18_s0, add_3_module_18_s1,
       add_3_module_18_s2, add_3_module_18_s3, add_3_module_19_s0, add_3_module_19_s1, add_3_module_19_s2,
       add_3_module_19_s3, add_3_module_20_s0, add_3_module_20_s1, add_3_module_20_s2, add_3_module_21_s0,
       add_3_module_21_s1, add_3_module_21_s2, add_3_module_22_s0, add_3_module_22_s1, add_3_module_22_s2,
       add_3_module_22_s3, add_3_module_23_s0, add_3_module_23_s1, add_3_module_23_s2, add_3_module_23_s3,
       add_3_module_24_s0, add_3_module_24_s1, add_3_module_24_s2, add_3_module_24_s3, add_3_module_25_s0,
       add_3_module_25_s1, add_3_module_25_s2, add_3_module_25_s3, add_3_module_26_s0, add_3_module_26_s1,
       add_3_module_26_s2, add_3_module_26_s3, add_3_module_27_s0, add_3_module_27_s1, add_3_module_27_s2,
       add_3_module_27_s3, add_3_module_28_s0, add_3_module_28_s1, add_3_module_28_s2, add_3_module_30_s0,
       add_3_module_30_s1, add_3_module_30_s2, add_3_module_30_s3, add_3_module_32_s0, add_3_module_32_s1,
       add_3_module_32_s2, add_3_module_32_s3;

  Add_3_Module add_3_module_1 (
    .A3(1'b0), .A2(_16bit_Input[15]), .A1(_16bit_Input[14]), .A0(_16bit_Input[13]), .S3(add_3_module_1_s3),
    .S2(add_3_module_1_s2), .S1(add_3_module_1_s1), .S0(add_3_module_1_s0));
  Add_3_Module add_3_module_2 (
    .A3(add_3_module_1_s2), .A2(add_3_module_1_s1), .A1(add_3_module_1_s0), .A0(_16bit_Input[12]),
    .S3(add_3_module_2_s3), .S2(add_3_module_2_s2), .S1(add_3_module_2_s1), .S0(add_3_module_2_s0));
  Add_3_Module add_3_module_3 (
    .A3(add_3_module_2_s2), .A2(add_3_module_2_s1), .A1(add_3_module_2_s0), .A0(_16bit_Input[11]),
    .S3(add_3_module_3_s3), .S2(add_3_module_3_s2), .S1(add_3_module_3_s1), .S0(add_3_module_3_s0));
  Add_3_Module add_3_module_4 (
    .A3(add_3_module_3_s2), .A2(add_3_module_3_s1), .A1(add_3_module_3_s0), .A0(_16bit_Input[10]),
    .S3(add_3_module_4_s3), .S2(add_3_module_4_s2), .S1(add_3_module_4_s1), .S0(add_3_module_4_s0));
  Add_3_Module add_3_module_5 (
    .A3(1'b0), .A2(add_3_module_1_s3), .A1(add_3_module_2_s3), .A0(add_3_module_3_s3),
    .S3(add_3_module_5_s3), .S2(add_3_module_5_s2), .S1(add_3_module_5_s1), .S0(add_3_module_5_s0));
  Add_3_Module add_3_module_6 (
    .A3(add_3_module_5_s2), .A2(add_3_module_5_s1), .A1(add_3_module_5_s0), .A0(add_3_module_4_s3),
    .S3(add_3_module_6_s3), .S2(add_3_module_6_s2), .S1(add_3_module_6_s1), .S0(add_3_module_6_s0));
  Add_3_Module add_3_module_7 (
    .A3(add_3_module_4_s2), .A2(add_3_module_4_s1), .A1(add_3_module_4_s0), .A0(_16bit_Input[9]),
    .S3(add_3_module_7_s3), .S2(add_3_module_7_s2), .S1(add_3_module_7_s1), .S0(add_3_module_7_s0));
  Add_3_Module add_3_module_8 (
    .A3(add_3_module_7_s2), .A2(add_3_module_7_s1), .A1(add_3_module_7_s0), .A0(_16bit_Input[8]),
    .S3(add_3_module_8_s3), .S2(add_3_module_8_s2), .S1(add_3_module_8_s1), .S0(add_3_module_8_s0));
  Add_3_Module add_3_module_9 (
    .A3(1'b0), .A2(add_3_module_5_s3), .A1(add_3_module_6_s3), .A0(add_3_module_10_s3),
    .S3(add_3_module_9_s3), .S2(add_3_module_9_s2), .S1(add_3_module_9_s1), .S0(add_3_module_9_s0));
  Add_3_Module add_3_module_10 (
    .A3(add_3_module_6_s2), .A2(add_3_module_6_s1), .A1(add_3_module_6_s0), .A0(add_3_module_7_s3),
    .S3(add_3_module_10_s3), .S2(add_3_module_10_s2), .S1(add_3_module_10_s1), .S0(add_3_module_10_s0));
  Add_3_Module add_3_module_11 (
    .A3(add_3_module_10_s2), .A2(add_3_module_10_s1), .A1(add_3_module_10_s0), .A0(add_3_module_8_s3),
    .S3(add_3_module_11_s3), .S2(add_3_module_11_s2), .S1(add_3_module_11_s1), .S0(add_3_module_11_s0));
  Add_3_Module add_3_module_12 (
    .A3(add_3_module_8_s2), .A2(add_3_module_8_s1), .A1(add_3_module_8_s0), .A0(_16bit_Input[7]),
    .S3(add_3_module_12_s3), .S2(add_3_module_12_s2), .S1(add_3_module_12_s1), .S0(add_3_module_12_s0));
  Add_3_Module add_3_module_13 (
    .A3(add_3_module_12_s2), .A2(add_3_module_12_s1), .A1(add_3_module_12_s0), .A0(_16bit_Input[6]),
    .S3(add_3_module_13_s3), .S2(add_3_module_13_s2), .S1(add_3_module_13_s1), .S0(add_3_module_13_s0));
  Add_3_Module add_3_module_14 (
    .A3(add_3_module_9_s2), .A2(add_3_module_9_s1), .A1(add_3_module_9_s0), .A0(add_3_module_11_s3),
    .S3(add_3_module_14_s3), .S2(add_3_module_14_s2), .S1(add_3_module_14_s1), .S0(add_3_module_14_s0));
  Add_3_Module add_3_module_15 (
    .A3(add_3_module_14_s2), .A2(add_3_module_14_s1), .A1(add_3_module_14_s0), .A0(add_3_module_16_s3),
    .S3(add_3_module_15_s3), .S2(add_3_module_15_s2), .S1(add_3_module_15_s1), .S0(add_3_module_15_s0));
  Add_3_Module add_3_module_16 (
    .A3(add_3_module_11_s2), .A2(add_3_module_11_s1), .A1(add_3_module_11_s0), .A0(add_3_module_12_s3),
    .S3(add_3_module_16_s3), .S2(add_3_module_16_s2), .S1(add_3_module_16_s1), .S0(add_3_module_16_s0));
  Add_3_Module add_3_module_17 (
    .A3(add_3_module_16_s2), .A2(add_3_module_16_s1), .A1(add_3_module_16_s0), .A0(add_3_module_13_s3),
    .S3(add_3_module_17_s3), .S2(add_3_module_17_s2), .S1(add_3_module_17_s1), .S0(add_3_module_17_s0));
  Add_3_Module add_3_module_18 (
    .A3(add_3_module_13_s2), .A2(add_3_module_13_s1), .A1(add_3_module_13_s0), .A0(_16bit_Input[5]),
    .S3(add_3_module_18_s3), .S2(add_3_module_18_s2), .S1(add_3_module_18_s1), .S0(add_3_module_18_s0));
  Add_3_Module add_3_module_19 (
    .A3(add_3_module_18_s2), .A2(add_3_module_18_s1), .A1(add_3_module_18_s0), .A0(_16bit_Input[4]),
    .S3(add_3_module_19_s3), .S2(add_3_module_19_s2), .S1(add_3_module_19_s1), .S0(add_3_module_19_s0));
  Add_3_Module add_3_module_20 (
    .A3(1'b0), .A2(add_3_module_9_s3), .A1(add_3_module_14_s3), .A0(add_3_module_15_s3),
    .S2(add_3_module_20_s2), .S1(add_3_module_20_s1), .S0(add_3_module_20_s0));  // open: S3
  Add_3_Module add_3_module_21 (
    .A3(add_3_module_20_s2), .A2(add_3_module_20_s1), .A1(add_3_module_20_s0), .A0(add_3_module_22_s3),
    .S2(add_3_module_21_s2), .S1(add_3_module_21_s1), .S0(add_3_module_21_s0));  // open: S3
  Add_3_Module add_3_module_22 (
    .A3(add_3_module_15_s2), .A2(add_3_module_15_s1), .A1(add_3_module_15_s0), .A0(add_3_module_17_s3),
    .S3(add_3_module_22_s3), .S2(add_3_module_22_s2), .S1(add_3_module_22_s1), .S0(add_3_module_22_s0));
  Add_3_Module add_3_module_23 (
    .A3(add_3_module_22_s2), .A2(add_3_module_22_s1), .A1(add_3_module_22_s0), .A0(add_3_module_24_s3),
    .S3(add_3_module_23_s3), .S2(add_3_module_23_s2), .S1(add_3_module_23_s1), .S0(add_3_module_23_s0));
  Add_3_Module add_3_module_24 (
    .A3(add_3_module_17_s2), .A2(add_3_module_17_s1), .A1(add_3_module_17_s0), .A0(add_3_module_18_s3),
    .S3(add_3_module_24_s3), .S2(add_3_module_24_s2), .S1(add_3_module_24_s1), .S0(add_3_module_24_s0));
  Add_3_Module add_3_module_25 (
    .A3(add_3_module_24_s2), .A2(add_3_module_24_s1), .A1(add_3_module_24_s0), .A0(add_3_module_19_s3),
    .S3(add_3_module_25_s3), .S2(add_3_module_25_s2), .S1(add_3_module_25_s1), .S0(add_3_module_25_s0));
  Add_3_Module add_3_module_26 (
    .A3(add_3_module_19_s2), .A2(add_3_module_19_s1), .A1(add_3_module_19_s0), .A0(_16bit_Input[3]),
    .S3(add_3_module_26_s3), .S2(add_3_module_26_s2), .S1(add_3_module_26_s1), .S0(add_3_module_26_s0));
  Add_3_Module add_3_module_27 (
    .A3(add_3_module_26_s2), .A2(add_3_module_26_s1), .A1(add_3_module_26_s0), .A0(_16bit_Input[2]),
    .S3(add_3_module_27_s3), .S2(add_3_module_27_s2), .S1(add_3_module_27_s1), .S0(add_3_module_27_s0));
  Add_3_Module add_3_module_28 (
    .A3(add_3_module_21_s2), .A2(add_3_module_21_s1), .A1(add_3_module_21_s0), .A0(add_3_module_23_s3),
    .S2(add_3_module_28_s2), .S1(add_3_module_28_s1), .S0(add_3_module_28_s0));  // open: S3
  Add_3_Module add_3_module_29 (
    .A3(add_3_module_28_s2), .A2(add_3_module_28_s1), .A1(add_3_module_28_s0), .A0(add_3_module_30_s3),
    .S2(out_2[3]), .S1(out_2[2]), .S0(out_2[1]));  // open: S3
  Add_3_Module add_3_module_30 (
    .A3(add_3_module_23_s2), .A2(add_3_module_23_s1), .A1(add_3_module_23_s0), .A0(add_3_module_25_s3),
    .S3(add_3_module_30_s3), .S2(add_3_module_30_s2), .S1(add_3_module_30_s1), .S0(add_3_module_30_s0));
  Add_3_Module add_3_module_31 (
    .A3(add_3_module_30_s2), .A2(add_3_module_30_s1), .A1(add_3_module_30_s0), .A0(add_3_module_32_s3),
    .S3(out_2[0]), .S2(out_3[3]), .S1(out_3[2]), .S0(out_3[1]));
  Add_3_Module add_3_module_32 (
    .A3(add_3_module_25_s2), .A2(add_3_module_25_s1), .A1(add_3_module_25_s0), .A0(add_3_module_26_s3),
    .S3(add_3_module_32_s3), .S2(add_3_module_32_s2), .S1(add_3_module_32_s1), .S0(add_3_module_32_s0));
  Add_3_Module add_3_module_33 (
    .A3(add_3_module_32_s2), .A2(add_3_module_32_s1), .A1(add_3_module_32_s0), .A0(add_3_module_27_s3),
    .S3(out_3[0]), .S2(out_4[3]), .S1(out_4[2]), .S0(out_4[1]));
  Add_3_Module add_3_module_34 (
    .A3(add_3_module_27_s2), .A2(add_3_module_27_s1), .A1(add_3_module_27_s0), .A0(_16bit_Input[1]),
    .S3(out_4[0]), .S2(out_5[3]), .S1(out_5[2]), .S0(out_5[1]));

  assign out_5[0] = _16bit_Input[0];
endmodule
